// Logisim project map_circus.circ as structural Verilog: 1 circuit, main circuit map_loader
module map_loader (
  output [29:0] out_reg1,
  output [29:0] out_reg2,
  output [29:0] out_reg3,
  output [29:0] out_reg4,
  output [29:0] out_reg5,
  output [29:0] out_reg6,
  output [1:0] map_num,
  output [29:0] out_reg7,
  output [29:0] out_reg8,
  output map_gen,
  output [29:0] out_reg9,
  output [29:0] out_reg10,
  output [29:0] out_reg11,
  output [29:0] out_reg12,
  output [29:0] out_reg13,
  output [29:0] out_reg14,
  output [29:0] out_reg15,
  output [29:0] out_reg16,
  output [29:0] out_reg17,
  output [29:0] out_reg18,
  output [29:0] out_reg19,
  output [29:0] out_reg20,
  output [29:0] out_reg21,
  output [29:0] out_reg22,
  output [29:0] out_reg23,
  output [29:0] out_reg24,
  output [29:0] out_reg25,
  output [29:0] out_reg26,
  output [29:0] out_reg27,
  output [29:0] out_reg28,
  output [29:0] out_reg29,
  output [29:0] out_reg30
);

  wire power_map_1, power_map_2, power_map_3, power_map_4;
  wire [4:0] reg_adr;

  Counter #(.width(5), .max('h1c)) counter_1 (.Q(reg_adr), .clk(map_gen));  // open: load, D, count, carry, clr
  ROM #(.addrWidth(5), .dataWidth(30)) rom_1 (.addr(reg_adr), .data(out_reg2), .sel(power_map_1));
  ROM #(.addrWidth(5), .dataWidth(30)) rom_2 (.addr(reg_adr), .data(out_reg2), .sel(power_map_2));
  ROM #(.addrWidth(5), .dataWidth(30)) rom_3 (.addr(reg_adr), .data(out_reg2), .sel(power_map_3));
  ROM #(.addrWidth(5), .dataWidth(30)) rom_4 (.addr(reg_adr), .data(out_reg2), .sel(power_map_4));
  Decoder #(.select(2), .enable("false")) decoder_1 (
    .out0(power_map_1), .out1(power_map_2), .out2(power_map_3), .out3(power_map_4), .sel(map_num));

  assign out_reg3 = out_reg2;
  assign out_reg4 = out_reg2;
  assign out_reg5 = out_reg2;
  assign out_reg6 = out_reg2;
  assign out_reg7 = out_reg2;
  assign out_reg8 = out_reg2;
  assign out_reg9 = out_reg2;
  assign out_reg10 = out_reg2;
  assign out_reg11 = out_reg2;
  assign out_reg12 = out_reg2;
  assign out_reg13 = out_reg2;
  assign out_reg14 = out_reg2;
  assign out_reg15 = out_reg2;
  assign out_reg16 = out_reg2;
  assign out_reg17 = out_reg2;
  assign out_reg18 = out_reg2;
  assign out_reg19 = out_reg2;
  assign out_reg20 = out_reg2;
  assign out_reg21 = out_reg2;
  assign out_reg22 = out_reg2;
  assign out_reg23 = out_reg2;
  assign out_reg24 = out_reg2;
  assign out_reg25 = out_reg2;
  assign out_reg26 = out_reg2;
  assign out_reg27 = out_reg2;
  assign out_reg28 = out_reg2;
  assign out_reg29 = out_reg2;
  assign out_reg30 = out_reg2;

  // Notes on the sheet:
  //   contents of rom_1 (hex, n*v repeats v):
  //   11111111 30*10000001 11111111
  //   contents of rom_2 (hex, n*v repeats v):
  //   28*0 123 0 0 123
endmodule
